# Fritzing sketch Sketch (saved by Fritzing 0.9.3b)

parts:
  Часть1 = Arduino Nano (Rev3.0)
  7_Segment3 = 7 Segment Display
  7_Segment2 = 7 Segment Display
  7_Segment1 = 7 Segment Display
  Q1 = MOSFET-NCHANNEL [package=to220v]
  R1 = Resistor [tolerance=±5% resistance=100 package=THT]
  R2 = Resistor [tolerance=±5% resistance=1k package=THT]
  U1 = LM358 [package=dip08]
  R3 = Resistor [tolerance=±5% resistance=10k package=THT]  # not connected
  C1 = Electrolytic Capacitor [capacitance=0.1mF package="100 mil [THT, electrolytic]"]
  R4 = Resistor [tolerance=±5% resistance=130k package=THT]
  R5 = Resistor [tolerance=±5% resistance=1k package=THT]
  C2 = Electrolytic Capacitor [capacitance=0.1mF package="100 mil [THT, electrolytic]"]

nets:
  N1: Часть1.D5, R1.Pin_0, R2.Pin_1
  N2: Часть1.D11/MOSI, 7_Segment1.common_cathode
  N3: Часть1.D12/MISO, 7_Segment2.common_cathode
  N4: Часть1.A7, R4.Pin_1, C2.+
  N5: Часть1.D13/SCK, 7_Segment3.common_cathode
  N6: Q1.G, R1.Pin_1
  N7: U1.G$1_-IN, R5.Pin_1
  N8: U1.G$1_V-, C1.+, R5.Pin_0

notes:
  0
  19V
  Out 5V
  In 19V
  PWM
  IRFZ44N
  R=1K
  R=100
  temp control
  t   sensor
  1K
  130K
  10K
  0.1mF
  lm358
